# Fritzing sketch dynamixel_tentacle (saved by Fritzing 0.9.3b)
stripboards: 1

parts:
  Part1 = Arduino Uno (Rev3)
  U2 = SLIDER [package=slider]
  LED1 = smd LED [color="Red (633nm)" package="0603 [SMD]"]
  LED2 = smd LED [color="Red (633nm)" package="0603 [SMD]"]
  LED3 = smd LED [color="Red (633nm)" package="0603 [SMD]"]
  R3 = Resistor [tolerance=±5% power=0.25 resistance=330 package=THT]
  R4 = Resistor [tolerance=±5% power=0.25 resistance=330 package=THT]
  R5 = Resistor [tolerance=±5% power=0.25 resistance=330 package=THT]
  U3 = SLIDER [package=slider]
  U4 = SLIDER [package=slider]
  servo1 = Dagu DGServo 9g header connector (female) [package=THT]
  servo3 = Dagu DGServo 9g header connector (female) [package=THT]
  servo2 = Dagu DGServo 9g header connector (female) [package=THT]
  V1 = DC Power [voltage=7.5]
  9-12V = Power Jack [package=power_jack_smd]
  U7 = Molex Picoblade Series Header [part_number="DFrobot Dynamixel servo shield " package=Picoblade-53261-0319]
  S2 = Round Pushbutton
  LED4 = smd LED [color="Red (633nm)" package="1206 [SMD]"]
  microSD1 = MicroSD Card Module
  ZS-042_RTC1 = ZS-042 RTC Module

nets:
  N1: Part1.A1, U3.S
  N2: Part1.A2, U4.S
  N3: Part1.A3, U2.S
  N4: Part1.A4/SDA, ZS-042_RTC1.SDA
  N5: Part1.A5/SCL, ZS-042_RTC1.SCL
  N6: Part1.D8, S2.leg1
  N7: Part1.D9_PWM, LED4.anode
  N8: Part1.D11_PWM/MOSI, microSD1.MOSI
  N9: Part1.D12/MISO, microSD1.MISO
  N10: Part1.D13/SCK, microSD1.SCK
  GND: Part1.GND, U2.A, R3.Pin_1, R4.Pin_1, R5.Pin_1, U3.A, U4.A, servo1.gnd, servo3.gnd, servo2.gnd, 9-12V.GNDBREAK, U7.3, S2.leg0, LED4.cathode, microSD1.GND, ZS-042_RTC1.GND
  N11: Part1.D4, microSD1.CS
  N12: Part1.D5_PWM, LED1.anode
  N13: Part1.D6_PWM, LED2.anode
  N14: Part1.D7, LED3.anode
  3V3: Part1.3V3, ZS-042_RTC1.VCC
  5V: Part1.5V, U2.E, U3.E, U4.E, microSD1.VCC
  N15: LED1.cathode, R4.Pin_0
  N16: LED2.cathode, R5.Pin_0
  N17: LED3.cathode, R3.Pin_0
  VCC: servo1.Vcc, servo3.Vcc, servo2.Vcc, U7.2
  N18: servo1.pulse, servo3.pulse, servo2.pulse, U7.1
  N19: V1.V+, 9-12V.PWR
  N20: V1.V-, 9-12V.GND
